# Fritzing sketch Sketch (saved by Fritzing 0.9.3b)
breadboards: 2

parts:
  元件1 = Arduino Uno (Rev3)
  Disp1 = LBT2088AH [part_number=LBT2088AH]
  元件2 = Bluetooth HC-05 Macho

nets:
  N1: 元件1.A0, Disp1.pin_6
  N2: 元件1.A1, Disp1.pin_11
  N3: 元件1.A2, Disp1.pin_15
  N4: 元件1.A3, Disp1.pin_16
  N5: 元件1.A4/SDA, 元件2.RXD
  N6: 元件1.A5/SCL, 元件2.TXD
  N7: 元件1.D8, Disp1.pin_14
  N8: 元件1.D9_PWM, Disp1.pin_9
  N9: 元件1.D10_PWM/SS, Disp1.pin_13
  N10: 元件1.D11_PWM/MOSI, Disp1.pin_3
  N11: 元件1.D12/MISO, Disp1.pin_4
  N12: 元件1.D13/SCK, Disp1.pin_10
  N13: 元件1.D2, Disp1.pin_5
  N14: 元件1.D3_PWM, Disp1.pin2
  N15: 元件1.D4, Disp1.pin_7
  N16: 元件1.D5_PWM, Disp1.pin1
  N17: 元件1.D6_PWM, Disp1.pin_12
  N18: 元件1.D7, Disp1.pin_8
  N19: 元件1.3V3, 元件2.Key
  5V: 元件1.5V, 元件2.VCC
  GND: 元件1.GND, 元件2.GND

notes:
  key接3.3v進AT (:

// code stored in the sketch: main.ino
#include <avr/pgmspace.h>
#include <SoftwareSerial.h>
#include <Wire.h>
const int line[]={2,3,4,5,6,7,8,9};
const int column[]={10,11,12,13,A0,A1,A2,A3};
//frame using flash memory
const bool frame[8][40] PROGMEM={
    {0,0,0,0,0,0,0,0,0,1,0,0,0,0,0,0,0,0,0,0,0,0,0,0,0,0,0,0,0,0,0,0,0,0,0,0,0,0,0,0},
    {0,0,1,0,1,1,0,0,0,0,0,0,0,0,0,0,0,0,0,0,0,0,0,0,0,0,1,0,0,0,1,1,1,0,0,0,0,0,0,0},
    {0,0,1,1,0,0,1,0,1,1,0,0,0,0,1,1,1,0,0,0,1,1,1,0,0,1,1,0,0,1,0,0,0,1,0,0,0,0,0,0},
    {0,0,1,0,0,0,1,0,0,1,0,0,0,1,0,0,0,1,0,1,0,0,0,1,0,0,1,0,0,1,1,1,1,1,0,0,0,0,0,0},
    {0,0,1,0,0,0,1,0,0,1,0,0,0,1,0,0,0,1,0,1,0,0,0,1,0,0,1,0,0,1,0,0,0,0,0,0,0,0,0,0},
    {0,0,1,0,0,0,1,0,0,1,0,0,0,0,1,1,1,1,0,0,1,1,1,1,0,0,1,0,0,1,0,0,0,0,0,0,0,0,0,0},
    {0,0,1,0,0,0,1,0,1,1,1,0,0,0,0,0,0,1,0,0,0,0,0,1,0,0,1,0,0,0,1,1,1,1,0,0,0,0,0,0},
    {0,0,0,0,0,0,0,0,0,0,0,0,0,1,1,1,1,0,0,1,1,1,1,0,1,1,1,1,1,0,0,0,0,0,0,0,0,0,0,0}
};
double pos=0.0;
int led_displayID=0;
//f* you BTS stans on Twitter
SoftwareSerial bts(A4,A5);
void def_display();
void bluetooh();
void setup() {
    Serial.begin(9600);
    Serial.println("TEST MESSAGE");
    //HC-05 default speed
    bts.begin(38400);
	for(int i=0;i<8;i++){
        pinMode(line[i],OUTPUT);
        pinMode(column[i],OUTPUT);
        digitalWrite(line[i],LOW);
        digitalWrite(column[i],HIGH);
    }
}
void loop() {
    switch (led_displayID){
        case 0:
            def_display();
            break;
        default:
            break;
    }
    
    
}
void def_display(){
    for(int l=0;l<8;l++){
        for(int c=0;c<8;c++){
            static int frame_buf=pgm_read_byte_near(&frame[c][l+(int)(floor(pos))]);
            if(frame_buf==1){
                digitalWrite(line[l],HIGH);
                digitalWrite(column[c],LOW);
                delay(2);
                digitalWrite(line[l],LOW);
                digitalWrite(column[c],HIGH);
            }else if(frame_buf==0){
                delay(2);
            }
            pos+=0.02;
        }
    }
    if(pos>=39.0){
        pos=0.0;
    }
}
void bluetooth(){

}
/*int supersonic_func1(){
    digitalWrite(trig,LOW);
    delayMicroseconds(2);
    digitalWrite(trig,HIGH);
    delayMicroseconds(10);
    digitalWrite(trig,LOW);
    /*
    v=340 m/s
    t=s/v
    s=t*0.034/2
    */
    /*duration=pulseIn(echo,HIGH);
    distance= duration*0.034/2;
    Serial.println(distance);
}*/
/*const int frame[8][40]={
    {0,0,0,0,0,0,0,0,0,0,0,0,0,0,0,0,0,0,0,0,0,0,0,0,0,0,0,0,0,0,0,0,0,0,0,0,0,0,0,0},
    {0,0,0,0,0,0,0,0,0,0,0,0,0,0,0,0,0,0,0,0,0,0,0,0,0,0,0,0,0,0,0,0,0,0,0,0,0,0,0,0},
    {0,0,0,0,0,0,0,0,0,0,0,0,0,0,0,0,0,0,0,0,0,0,0,0,0,0,0,0,0,0,0,0,0,0,0,0,0,0,0,0},
    {0,0,0,0,0,0,0,0,0,0,0,0,0,0,0,0,0,0,0,0,0,0,0,0,0,0,0,0,0,0,0,0,0,0,0,0,0,0,0,0},
    {0,0,0,0,0,0,0,0,0,0,0,0,0,0,0,0,0,0,0,0,0,0,0,0,0,0,0,0,0,0,0,0,0,0,0,0,0,0,0,0},
    {0,0,0,0,0,0,0,0,0,0,0,0,0,0,0,0,0,0,0,0,0,0,0,0,0,0,0,0,0,0,0,0,0,0,0,0,0,0,0,0},
    {0,0,0,0,0,0,0,0,0,0,0,0,0,0,0,0,0,0,0,0,0,0,0,0,0,0,0,0,0,0,0,0,0,0,0,0,0,0,0,0},
    {0,0,0,0,0,0,0,0,0,0,0,0,0,0,0,0,0,0,0,0,0,0,0,0,0,0,0,0,0,0,0,0,0,0,0,0,0,0,0,0}
}*/
